# Fritzing sketch maccanumBotNotWireless (saved by Fritzing 0.9.3b)
breadboards: 1

parts:
  Part1 = Adafruit Motor/Stepper/Servo Shield [part_number="Adafruit #1438"]
  Part2 = Thumb Joystick
  S1 = Round Pushbutton
  S2 = Round Pushbutton
  S3 = Round Pushbutton
  S4 = Round Pushbutton
  S5 = Round Pushbutton
  S6 = Round Pushbutton
  S7 = Toggle Switch spst [package=THT]
  M2 = DC Motor
  M3 = DC Motor
  U1 = POT [package=pot_mammoth]
  M5 = DC Motor
  M6 = DC Motor

nets:
  N1: Part1.M2A, M6.pin_1
  N2: Part1.M2B, M6.pin_2
  N3: Part1.M1B, M3.pin_1
  N4: Part1.M1A, M3.pin_2
  N5: Part1.M3A, M2.pin_2
  N6: Part1.M3B, M2.pin_1
  N7: Part1.M4B, M5.pin_2
  N8: Part1.M4A, M5.pin_1
  +5V: Part1.+5V, Part2.VCC, U1.S
  GND: Part1.GND, Part2.GND, S1.leg1, S2.leg1, S3.leg1, S4.leg1, S5.leg1, S6.leg1, U1.E
  N9: Part1.VMOTOR, S7.COM
  N10: Part1.AD0, Part2.HORZ
  N11: Part1.AD1, Part2.VERT
  N12: Part1.AD2, U1.A
  N13: Part1.D0, S1.leg0
  N14: Part1.D1, S2.leg0
  N15: Part1.D2, S3.leg0
  N16: Part1.D3, S4.leg0
  N17: Part1.D4, S5.leg0
  N18: Part1.D5, S6.leg0
  N19: Part1.D6, Part2.SEL

notes:
  Battery 12Volts

custom parts:
  Adafruit Motor/Stepper/Servo Shield: The original Adafruit Motorshield kit is one of our most beloved kits, which is why we decided to make something even better. We have upgraded the shield kit to make the bestest, easiest way to drive DC and Stepper motors. This shield will make quick work of your next robotics project! We kept the ability to drive up to 4 DC motors or 2 stepper motors, but added many improvements: Instead of a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
  Toggle Switch spst: Toggle Switch single pole single throw
